# Fritzing sketch CircuitDiagram (saved by Fritzing 0.9.3b)
breadboards: 1

parts:
  Part1 = Arduino Uno (Rev3)
  J1 = Infrared Proximity Sensor
  J2 = Basic Servo
  J3 = Basic Servo

nets:
  N1: Part1.A0, J1.Vout
  N2: Part1.D9_PWM, J2.pulse
  N3: Part1.D10_PWM/SS, J3.pulse
  GND: Part1.GND, J1.GND, J2.gnd, J3.gnd
  VCC: Part1.5V, J1.Vcc, J2.vcc, J3.vcc
